# Fritzing sketch fritzingvending-breadboard (saved by Fritzing 0.9.4)
breadboards: 1

parts:
  Raspberry_Pi_1 = Raspberry Pi 3 [part_number=RPI-3-V1.2]  # not connected
  Onderdeel1 = Coin Acceptor - 6-Coin version
  Load_Cell1 = Load Cell - Red/white/black/green
  U1 = LCD-16X2 [package=lcd-16x2_noholes]
  Onderdeel2 = Adafruit T-Cobbler Plus [part_number="Adafruit #1989 and #2028"]
  Onderdeel3 = SparkFun Load Sensor Combinator
  J1 = Basic Servo
  R2 = Trimmer Potentiometer [maximum_resistance=10kΩ package=THT]
  R1 = Temperature Sensor (Thermistor) [thermistor_type=NTC package=THT]
  R3 = Resistor [tolerance=±5% resistance=10k package="2010 [SMD]"]
  Keypad4x1 = Keypad Membran 4x4

nets:
  GND: Onderdeel1.GND, J1.gnd
  N1: Onderdeel1.SIG, Onderdeel2.GPIO17
  12V: Onderdeel1.12V, J1.vcc
  N2: Load_Cell1.wire1, Onderdeel3.E+
  N3: Load_Cell1.wire2, Onderdeel3.A-
  N4: Load_Cell1.wire3, Onderdeel3.E-
  N5: Load_Cell1.wire4, Onderdeel3.A+
  GND_2: U1.VSS, U1.R_W, U1.K, Onderdeel2.GND, Onderdeel3.GND, R2.leg2, R1.pin_1
  VDD: U1.VDD, U1.A, Onderdeel2.+5V, Onderdeel3.5V, R2.leg1, R3.Pin_1
  N6: U1.VO, R2.wiper
  N7: U1.RS, Onderdeel2.GPIO12
  N8: U1.E, Onderdeel2.GPIO25
  N9: U1.DB0, Onderdeel2.GPIO24
  N10: U1.DB1, Onderdeel2.GPIO23
  N11: U1.DB2, Onderdeel2.GPIO18
  N12: U1.DB3, Onderdeel2.RXD
  N13: Onderdeel2.MOSI, Keypad4x1.Pin8
  N14: Onderdeel2.MISO, Keypad4x1.Pin7
  N15: Onderdeel2.SCLK, Keypad4x1.Pin6
  N16: Onderdeel2.EEDAT, R1.pin_0, R3.Pin_0
  N17: Onderdeel2.GPIO5, Keypad4x1.Pin5
  N18: Onderdeel2.GPIO6, Keypad4x1.Pin4
  N19: Onderdeel2.GPIO13, Keypad4x1.Pin3
  N20: Onderdeel2.GPIO19, Keypad4x1.Pin2
  N21: Onderdeel2.GPIO26, Keypad4x1.Pin1
  N22: Onderdeel2.GPIO16, Onderdeel3.TEMP_DAT
  N23: Onderdeel2.GPIO20, J1.rx
  N24: Onderdeel2.GPIO21, J1.tx

notes:
  12V DC Power Supply

custom parts:
  Coin Acceptor - 6-Coin version: 12V coin acceptor that can handle up to 6 different denominations. Output is either pulse width, serial, or single pin per coin value.
  Load Cell - Red/white/black/green: A rectangle load cell/weighting pressure Sensor with four wires - Red, white, black, green. Normally corresponding with E+, E-, A+, A- respectively.
  Adafruit T-Cobbler Plus: The Raspberry Pi has landed on the Maker World like a 40-GPIO pinned, quad-USB ported, credit card sized bomb of DIY joy. And while you can use most of our great Model B accessories by hooking up our downgrade cable, its probably a good time to upgrade your set up and accessorize using all of the 40 pins. That's why we now carry the Assembled Adafruit Pi T-Cobbler Plus - Breakout + Cable for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
  Basic Servo: A generic servo.
  Keypad Membran 4x4: Membrane Keypad 4x4 Matrix
