# Fritzing sketch fritzingvending-schematic (saved by Fritzing 0.9.4)
breadboards: 1

parts:
  Muntstuk_Acceptor = Coin Acceptor - 6-Coin version
  4x4_matrix_membrane_keypad = Keypad4x4
  Load_Cell = Load Cell - Red/white/black/green
  U1 = LCD-16X2 [package=lcd-16x2_noholes]
  Raspberry_Pi_-_T-Cobbler = Adafruit T-Cobbler Plus [part_number="Adafruit #1989 and #2028"]
  Servo = Basic Servo
  R2 = Trimmer Potentiometer [maximum_resistance=10kΩ package=THT]
  R1 = Temperature Sensor (Thermistor) [thermistor_type=NTC package=THT]
  R3 = Resistor [tolerance=±5% resistance=10k package="2010 [SMD]"]
  Load_Cell_Amplifier = HX711 Weighing Sensor Module

nets (from the schematic view):
  12V: Muntstuk_Acceptor.GND, Muntstuk_Acceptor.12V, Servo.rx
  N1: Muntstuk_Acceptor.SIG, Raspberry_Pi_-_T-Cobbler.GPIO17
  N2: 4x4_matrix_membrane_keypad.connector0, Raspberry_Pi_-_T-Cobbler.GPIO26
  N3: 4x4_matrix_membrane_keypad.connector1, Raspberry_Pi_-_T-Cobbler.GPIO19
  N4: 4x4_matrix_membrane_keypad.connector2, Raspberry_Pi_-_T-Cobbler.GPIO13
  N5: 4x4_matrix_membrane_keypad.connector4, Raspberry_Pi_-_T-Cobbler.GPIO6
  N6: 4x4_matrix_membrane_keypad.connector5, Raspberry_Pi_-_T-Cobbler.GPIO5
  N7: 4x4_matrix_membrane_keypad.connector6, Raspberry_Pi_-_T-Cobbler.SCLK
  N8: 4x4_matrix_membrane_keypad.connector7, Raspberry_Pi_-_T-Cobbler.MISO
  N9: 4x4_matrix_membrane_keypad.connector8, Raspberry_Pi_-_T-Cobbler.MOSI
  N10: Load_Cell.wire1, Load_Cell_Amplifier.E+
  N11: Load_Cell.wire2, Load_Cell_Amplifier.A-
  N12: Load_Cell.wire3, Load_Cell_Amplifier.E-
  N13: Load_Cell.wire4, Load_Cell_Amplifier.A+
  VSS: U1.VSS, U1.R_W, U1.K, Raspberry_Pi_-_T-Cobbler.GND, R2.leg2, R1.pin_1
  VDD: U1.VDD, U1.A, Raspberry_Pi_-_T-Cobbler.+5V, R2.leg1, Load_Cell_Amplifier.VCC
  N14: U1.VO, R2.wiper
  N15: U1.RS, Raspberry_Pi_-_T-Cobbler.TXD
  N16: U1.E, Raspberry_Pi_-_T-Cobbler.RXD
  N17: U1.DB0, Raspberry_Pi_-_T-Cobbler.GPIO18
  N18: U1.DB1, Raspberry_Pi_-_T-Cobbler.GPIO23
  N19: U1.DB2, Raspberry_Pi_-_T-Cobbler.GPIO24
  N20: U1.DB3, Raspberry_Pi_-_T-Cobbler.GPIO25
  N21: Raspberry_Pi_-_T-Cobbler.SDA, Load_Cell_Amplifier.CK/TX
  N22: Raspberry_Pi_-_T-Cobbler.SCL, Load_Cell_Amplifier.DO/RX
  N23: Raspberry_Pi_-_T-Cobbler.GPIO22, R1.pin_0, R3.Pin_0
  N24: Raspberry_Pi_-_T-Cobbler.GPIO21, Servo.tx
  N25: R3.Pin_1, Load_Cell_Amplifier.GND

notes:
  12V DC Power Supply

custom parts:
  Coin Acceptor - 6-Coin version: 12V coin acceptor that can handle up to 6 different denominations. Output is either pulse width, serial, or single pin per coin value.
  Load Cell - Red/white/black/green: A rectangle load cell/weighting pressure Sensor with four wires - Red, white, black, green. Normally corresponding with E+, E-, A+, A- respectively.
  Adafruit T-Cobbler Plus: The Raspberry Pi has landed on the Maker World like a 40-GPIO pinned, quad-USB ported, credit card sized bomb of DIY joy. And while you can use most of our great Model B accessories by hooking up our downgrade cable, its probably a good time to upgrade your set up and accessorize using all of the 40 pins. That's why we now carry the Assembled Adafruit Pi T-Cobbler Plus - Breakout + Cable for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
  Basic Servo: A generic servo.
